# Fritzing sketch DataScience (saved by Fritzing 0.9.3b)
breadboards: 1

parts:
  Raspberry_Pi_1 = Raspberry Pi 3 [part_number=RPI-3-V1.2]
  S1 = Pushbutton [package="[THT]"]
  R1 = Resistor [tolerance=±5% resistance=220 package=THT]
  HC-SR04_Sensor_1 = HC-SR04 Ultrasonic Distance Sensor
  R2 = Resistor [tolerance=±5% resistance=220 package=THT]
  R3 = Resistor [tolerance=±5% resistance=220 package=THT]

nets:
  N1: Raspberry_Pi_1.3v3, R1.Pin_0
  GND: Raspberry_Pi_1.GND, S1.Pin_1, S1.Pin_2, HC-SR04_Sensor_1.GND, R2.Pin_1
  N2: Raspberry_Pi_1.GPIO24, R2.Pin_0, R3.Pin_0
  N3: Raspberry_Pi_1.GPIO23, HC-SR04_Sensor_1.TRIG
  5V: Raspberry_Pi_1.5V, HC-SR04_Sensor_1.VCC
  N4: S1.Pin_3, S1.Pin_4, R1.Pin_1
  N5: HC-SR04_Sensor_1.ECHO, R3.Pin_1
